// Logisim project trab_12_bit.circ as structural Verilog
module main (
);

  wire and_1_out, CLK, compare, cond, dado_breg, MUX_ULA, pc_sel, SINAL_CONTROL, WBREG;
  wire [2:0] func3, OPCODE, OPULA;
  wire [4:0] rom_1_data;
  wire [11:0] adder_1_out, banco_registradores_1_b, IMM, multiplexer_1_out, multiplexer_2_out,
       multiplexer_3_out, pc_imm, PC_q, RA, ram_1_dout, ula_1_c;

  Multiplexer #(.width(12)) multiplexer_1 (.in0(adder_1_out), .in1(pc_imm), .out(multiplexer_1_out), .sel(and_1_out));
  and and_1 (and_1_out, pc_sel, compare);
  Clock clock_1 (.out(CLK));
  Register #(.width(12)) PC (.D(multiplexer_1_out), .en(1'b1), .clk(CLK), .Q(PC_q));  // open: clr
  ROM #(.addrWidth(12), .dataWidth(12)) rom_1 (.addr(PC_q), .data({OPCODE, func3, cond, rom_1_data}));
  Adder #(.width(12)) adder_1 (.a(PC_q), .b(12'h1), .out(adder_1_out));  // open: cin, cout
  Adder #(.width(12)) adder_2 (.a(PC_q), .b(IMM), .out(pc_imm));  // open: cin, cout
  ROM #(.addrWidth(3)) rom_2 (.addr(OPCODE), .data({OPULA, WBREG, MUX_ULA, dado_breg, SINAL_CONTROL, pc_sel}));
  assign IMM = {{9{func3[2]}}, func3};  // Bit_Extender bit_extender_1
  BANCO_REGISTRADORES banco_registradores_1 (
    .D(multiplexer_2_out), .W(WBREG), .RS1(rom_1_data[3:2]), .RD({cond, rom_1_data[4]}), .CLK(CLK),
    .RS2(rom_1_data[1:0]), .A(RA), .B(banco_registradores_1_b));
  Multiplexer #(.width(12)) multiplexer_2 (.in0(ula_1_c), .in1(ram_1_dout), .out(multiplexer_2_out), .sel(dado_breg));
  Multiplexer #(.width(12)) multiplexer_3 (
    .in0(banco_registradores_1_b), .in1(IMM), .out(multiplexer_3_out), .sel(MUX_ULA));
  ULA ula_1 (.A(RA), .B(multiplexer_3_out), .FUNC3(func3), .OPULA(OPULA), .cond(cond), .C(ula_1_c), .COMPARE(compare));
  RAM #(.addrWidth(12), .dataWidth(12)) ram_1 (
    .addr(ula_1_c), .we(SINAL_CONTROL), .oe(1'b1), .clk(CLK), .din(banco_registradores_1_b), .dout(ram_1_dout));

  // Notes on the sheet:
  //   contents of rom_1 (hex, n*v repeats v):
  //   0 2fc 809 254 268 b67 2fc 809 254 268 b67
  //   pc+1
  //   PAD
  //   IMM
  //   contents of rom_2 (hex, n*v repeats v):
  //   10 38 58 9c aa e1
  //   R-TYPE
  //   RT
  //   RS
  //   RD
  //   FUNC3
  //   OPCODE
  //   I-TYPE
endmodule

module CLK (
  input  CLK_IN,
  input  CLK_ENB,
  input  MANUAL_CLK,
  input  HALT,
  output CLK_OUT
);

  wire and_1_out, and_2_out, not_1_out, not_2_out, or_1_out;

  not not_1 (not_1_out, HALT);
  not not_2 (not_2_out, CLK_ENB);
  and and_1 (and_1_out, CLK_IN, CLK_ENB);
  and and_2 (and_2_out, not_2_out, MANUAL_CLK);
  or or_1 (or_1_out, and_1_out, and_2_out);
  and and_3 (CLK_OUT, or_1_out, not_1_out);
endmodule

module PROGRAM_COUNTER (
  input  RESET,
  input  JUMP,
  input  COUNTER_ENABLE,
  input  CLOCK,
  input  [11:0] ADRESS_IN,
  input  COUNTER_OUT,
  output [11:0] ALWAYS_OUT,
  output [11:0] ADDRESS_OUT
);

  Counter #(.max('hfff), .width(12)) counter_1 (
    .clr(RESET), .load(JUMP), .up(COUNTER_ENABLE), .count(COUNTER_ENABLE), .clk(CLOCK), .D(ADRESS_IN),
    .Q(ALWAYS_OUT));  // open: carry
  assign ADDRESS_OUT = COUNTER_OUT ? ALWAYS_OUT : 12'bz;  // Controlled_Buffer controlled_buffer_1
endmodule

module ULA (
  input  [11:0] A,
  input  [11:0] B,
  input  [2:0] FUNC3,
  input  [2:0] OPULA,
  input  cond,
  output [11:0] C,
  output COMPARE
);

  wire comparator_2_eq, not_2_out;
  wire [2:0] multiplexer_1_out;
  wire [11:0] adder_1_out, and_1_out, not_1_out, or_1_out, shifter_1_out, shifter_2_out, subtractor_1_out,
       xor_1_out;

  assign not_1_out = ~B;  // NOT_Gate not_1, 12 bits wide
  Comparator #(.width(12)) comparator_1 (.a(A), .b(B));  // open: gt, eq, lt
  Adder #(.width(12)) adder_1 (.a(A), .b(B), .out(adder_1_out));  // open: cin, cout
  Subtractor #(.width(12)) subtractor_1 (.a(A), .b(B), .out(subtractor_1_out));  // open: bin, bout
  assign and_1_out = A & B;  // AND_Gate and_1, 12 bits wide
  assign or_1_out = A | B;  // OR_Gate or_1, 12 bits wide
  assign xor_1_out = A ^ B;  // XOR_Gate xor_1, 12 bits wide
  Shifter #(.width(12)) shifter_1 (.in(A), .\dist (B[3:0]), .out(shifter_1_out));
  Shifter #(.shift("lr"), .width(12)) shifter_2 (.in(A), .\dist (B[3:0]), .out(shifter_2_out));
  Multiplexer #(.select(3), .width(3)) multiplexer_1 (
    .in0(FUNC3), .in1(3'b000), .in2(3'b001), .in3(3'b000), .in4(3'b000), .in5(3'b000), .in6(3'b000),
    .in7(3'b000), .out(multiplexer_1_out), .sel(OPULA));
  Multiplexer #(.select(3), .width(12)) multiplexer_2 (
    .in0(adder_1_out), .in1(subtractor_1_out), .in2(and_1_out), .in3(or_1_out), .in4(xor_1_out),
    .in5(shifter_1_out), .in6(shifter_2_out), .in7(not_1_out), .out(C), .sel(multiplexer_1_out));
  Comparator #(.width(12)) comparator_2 (.a(B), .b(A), .eq(comparator_2_eq));  // open: gt, lt
  Multiplexer multiplexer_3 (.in0(comparator_2_eq), .in1(not_2_out), .out(COMPARE), .sel(cond));
  not not_2 (not_2_out, comparator_2_eq);
endmodule

module BANCO_REGISTRADORES (
  input  [11:0] D,
  input  W,
  input  [1:0] RS1,
  input  [1:0] RD,
  input  CLK,
  input  [1:0] RS2,
  output [11:0] A,
  output [11:0] B
);

  wire demultiplexer_1_out1, demultiplexer_1_out2, demultiplexer_1_out3;
  wire [11:0] multiplexer_1_out, multiplexer_2_out, multiplexer_3_out, R1_q, R2_q, R3_q;

  Demultiplexer #(.select(2)) demultiplexer_1 (
    .out1(demultiplexer_1_out1), .out2(demultiplexer_1_out2), .out3(demultiplexer_1_out3), .in(W), .sel(RD));  // open: out0
  Multiplexer #(.width(12)) multiplexer_1 (.in0(R1_q), .in1(D), .out(multiplexer_1_out), .sel(demultiplexer_1_out1));
  Multiplexer #(.width(12)) multiplexer_2 (.in0(R2_q), .in1(D), .out(multiplexer_2_out), .sel(demultiplexer_1_out2));
  Multiplexer #(.width(12)) multiplexer_3 (.in0(R3_q), .in1(D), .out(multiplexer_3_out), .sel(demultiplexer_1_out3));
  Register #(.width(12)) R1 (.D(multiplexer_1_out), .clk(CLK), .Q(R1_q));  // open: en, clr
  Register #(.width(12)) R2 (.D(multiplexer_2_out), .clk(CLK), .Q(R2_q));  // open: en, clr
  Register #(.width(12)) R3 (.D(multiplexer_3_out), .clk(CLK), .Q(R3_q));  // open: en, clr
  Multiplexer #(.select(2), .width(12)) multiplexer_4 (
    .in0({12{1'b0}}), .in1(R1_q), .in2(R2_q), .in3(R3_q), .out(A), .sel(RS1));
  Multiplexer #(.select(2), .width(12)) multiplexer_5 (
    .in0({12{1'b0}}), .in1(R1_q), .in2(R2_q), .in3(R3_q), .out(B), .sel(RS2));
endmodule

module MEM_INSTRUCOES (
);

  wire CLK;
  wire [11:0] adder_1_out, PC_q;

  Clock clock_1 (.out(CLK));
  Register #(.width(12)) PC (.D(adder_1_out), .en(1'b1), .clk(CLK), .Q(PC_q));  // open: clr
  Adder #(.width(12)) adder_1 (.a(PC_q), .b(12'h1), .out(adder_1_out));  // open: cin, cout
  ROM #(.addrWidth(12), .dataWidth(12)) rom_1 (.addr(PC_q));  // open: data

  // Notes on the sheet:
  //   contents of rom_1 (hex, n*v repeats v):
  //   16*0 121
endmodule

module BANCO_REGIS (
  input  [11:0] D,
  input  W,
  input  [2:0] RD,
  input  [2:0] RS1,
  input  CLK,
  input  [2:0] RS2,
  output [11:0] A,
  output [11:0] B
);

  wire demultiplexer_1_out1, demultiplexer_1_out2, demultiplexer_1_out3, demultiplexer_1_out4,
       demultiplexer_1_out5, demultiplexer_1_out6, demultiplexer_1_out7;
  wire [11:0] multiplexer_1_out, multiplexer_2_out, multiplexer_3_out, multiplexer_4_out, multiplexer_5_out,
       multiplexer_6_out, multiplexer_7_out, VR1, VR2, VR3, VR4, VR5, VR6, VR7;

  Demultiplexer #(.select(3)) demultiplexer_1 (
    .out1(demultiplexer_1_out1), .out2(demultiplexer_1_out2), .out3(demultiplexer_1_out3),
    .out4(demultiplexer_1_out4), .out5(demultiplexer_1_out5), .out6(demultiplexer_1_out6),
    .out7(demultiplexer_1_out7), .in(W), .sel(RD));  // open: out0
  Multiplexer #(.width(12)) multiplexer_1 (.in0(VR1), .in1(D), .out(multiplexer_1_out), .sel(demultiplexer_1_out1));
  Multiplexer #(.width(12)) multiplexer_2 (.in0(VR2), .in1(D), .out(multiplexer_2_out), .sel(demultiplexer_1_out2));
  Multiplexer #(.width(12)) multiplexer_3 (.in0(VR3), .in1(D), .out(multiplexer_3_out), .sel(demultiplexer_1_out3));
  Multiplexer #(.width(12)) multiplexer_4 (
    .in0(VR4), .out(multiplexer_4_out), .sel(demultiplexer_1_out4));  // open: in1
  Multiplexer #(.width(12)) multiplexer_5 (
    .in0(VR5), .out(multiplexer_5_out), .sel(demultiplexer_1_out5));  // open: in1
  Multiplexer #(.width(12)) multiplexer_6 (
    .in0(VR6), .out(multiplexer_6_out), .sel(demultiplexer_1_out6));  // open: in1
  Multiplexer #(.width(12)) multiplexer_7 (
    .in0(VR7), .out(multiplexer_7_out), .sel(demultiplexer_1_out7));  // open: in1
  Register #(.width(12)) R1 (.D(multiplexer_1_out), .clk(CLK), .Q(VR1));  // open: en, clr
  Register #(.width(12)) R2 (.D(multiplexer_2_out), .clk(CLK), .Q(VR2));  // open: en, clr
  Register #(.width(12)) R3 (.D(multiplexer_3_out), .clk(CLK), .Q(VR3));  // open: en, clr
  Register #(.width(12)) register_1 (.D(multiplexer_4_out), .clk(CLK), .Q(VR4));  // open: en, clr
  Register #(.width(12)) register_2 (.D(multiplexer_5_out), .clk(CLK), .Q(VR5));  // open: en, clr
  Register #(.width(12)) register_3 (.D(multiplexer_6_out), .clk(CLK), .Q(VR6));  // open: en, clr
  Register #(.width(12)) register_4 (.D(multiplexer_7_out), .clk(CLK), .Q(VR7));  // open: en, clr
  Multiplexer #(.select(3), .width(12)) multiplexer_8 (
    .in0({12{1'b0}}), .in1(VR1), .in2(VR2), .in3(VR3), .in4(VR4), .in5(VR5), .in6(VR6), .in7(VR7), .out(A),
    .sel(RS1));
  Multiplexer #(.select(3), .width(12)) multiplexer_9 (
    .in0({12{1'b0}}), .in1(VR1), .in2(VR2), .in3(VR3), .in4(VR4), .in5(VR5), .in6(VR6), .in7(VR7), .out(B),
    .sel(RS2));
endmodule

module BANCO_REGISTRADORES2 (
  input  [11:0] D,
  input  W,
  input  [1:0] RS1,
  input  [1:0] RD,
  input  CLK,
  input  [1:0] RS2,
  output [11:0] A,
  output [11:0] B
);

  wire demultiplexer_1_out0, demultiplexer_1_out1, demultiplexer_1_out2, demultiplexer_1_out3;
  wire [11:0] multiplexer_1_out, multiplexer_2_out, multiplexer_3_out, multiplexer_4_out, R0_q, R1_q, R2_q,
       R3_q;

  Demultiplexer #(.select(2)) demultiplexer_1 (
    .out0(demultiplexer_1_out0), .out1(demultiplexer_1_out1), .out2(demultiplexer_1_out2),
    .out3(demultiplexer_1_out3), .in(W), .sel(RD));
  Multiplexer #(.width(12)) multiplexer_1 (.in0(R0_q), .in1(D), .out(multiplexer_1_out), .sel(demultiplexer_1_out0));
  Multiplexer #(.width(12)) multiplexer_2 (.in0(R1_q), .in1(D), .out(multiplexer_2_out), .sel(demultiplexer_1_out1));
  Multiplexer #(.width(12)) multiplexer_3 (.in0(R2_q), .in1(D), .out(multiplexer_3_out), .sel(demultiplexer_1_out2));
  Multiplexer #(.width(12)) multiplexer_4 (.in0(R3_q), .in1(D), .out(multiplexer_4_out), .sel(demultiplexer_1_out3));
  Register #(.width(12)) R0 (.D(multiplexer_1_out), .clk(CLK), .Q(R0_q));  // open: en, clr
  Register #(.width(12)) R1 (.D(multiplexer_2_out), .clk(CLK), .Q(R1_q));  // open: en, clr
  Register #(.width(12)) R2 (.D(multiplexer_3_out), .clk(CLK), .Q(R2_q));  // open: en, clr
  Register #(.width(12)) R3 (.D(multiplexer_4_out), .clk(CLK), .Q(R3_q));  // open: en, clr
  Multiplexer #(.select(2), .width(12)) multiplexer_5 (
    .in0(R0_q), .in1(R1_q), .in2(R2_q), .in3(R3_q), .out(A), .sel(RS1));
  Multiplexer #(.select(2), .width(12)) multiplexer_6 (
    .in0(R0_q), .in1(R1_q), .in2(R2_q), .in3(R3_q), .out(B), .sel(RS2));
endmodule
